// Logisim project WITCPU.circ as structural Verilog: 1 circuit, main circuit main
module main (
  input  [15:0] DATA,
  input  [3:0] Rx,
  input  in_3,
  input  [3:0] RD,
  input  [3:0] Ry,
  output [15:0] out_6,
  output [15:0] out_7
);

  wire demultiplexer_1_out0, demultiplexer_1_out1, demultiplexer_1_out2, demultiplexer_1_out3,
       demultiplexer_1_out4, demultiplexer_1_out5, demultiplexer_1_out6, demultiplexer_1_out7,
       demultiplexer_1_out8, demultiplexer_1_out9, demultiplexer_1_out10, demultiplexer_1_out11,
       demultiplexer_1_out12, demultiplexer_1_out13, demultiplexer_1_out14, demultiplexer_1_out15;
  wire [15:0] R0_q, R1_q, R2_q, R3_q, R4_q, R5_q, R6_q, R7_q, R8_q, R9_q, Ra_q, Rb_q, Rc_q, Rd_q, Re_q, Rf_q;

  Demultiplexer #(.select(4)) demultiplexer_1 (
    .out0(demultiplexer_1_out0), .out1(demultiplexer_1_out1), .out2(demultiplexer_1_out2),
    .out3(demultiplexer_1_out3), .out4(demultiplexer_1_out4), .out5(demultiplexer_1_out5),
    .out6(demultiplexer_1_out6), .out7(demultiplexer_1_out7), .out8(demultiplexer_1_out8),
    .out9(demultiplexer_1_out9), .out10(demultiplexer_1_out10), .out11(demultiplexer_1_out11),
    .out12(demultiplexer_1_out12), .out13(demultiplexer_1_out13), .out14(demultiplexer_1_out14),
    .out15(demultiplexer_1_out15), .in(in_3), .sel(RD));  // open: en
  Register #(.width(16)) R0 (.D({16{1'b0}}), .Q(R0_q), .clk(demultiplexer_1_out0));  // open: en, clr
  Register #(.width(16)) R3 (.D(DATA), .Q(R3_q), .clk(demultiplexer_1_out3));  // open: en, clr
  Register #(.width(16)) R6 (.D(DATA), .Q(R6_q), .clk(demultiplexer_1_out6));  // open: en, clr
  Register #(.width(16)) R9 (.D(DATA), .Q(R9_q), .clk(demultiplexer_1_out9));  // open: en, clr
  Register #(.width(16)) Rc (.D(DATA), .Q(Rc_q), .clk(demultiplexer_1_out12));  // open: en, clr
  Register #(.width(16)) R1 (.D(DATA), .Q(R1_q), .clk(demultiplexer_1_out1));  // open: en, clr
  Register #(.width(16)) R4 (.D(DATA), .Q(R4_q), .clk(demultiplexer_1_out4));  // open: en, clr
  Register #(.width(16)) R7 (.D(DATA), .Q(R7_q), .clk(demultiplexer_1_out7));  // open: en, clr
  Register #(.width(16)) Ra (.D(DATA), .Q(Ra_q), .clk(demultiplexer_1_out10));  // open: en, clr
  Register #(.width(16)) u_Rd (.D(DATA), .Q(Rd_q), .clk(demultiplexer_1_out13));  // open: en, clr
  Register #(.width(16)) R2 (.D(DATA), .Q(R2_q), .clk(demultiplexer_1_out2));  // open: en, clr
  Register #(.width(16)) R5 (.D(DATA), .Q(R5_q), .clk(demultiplexer_1_out5));  // open: en, clr
  Register #(.width(16)) R8 (.D(DATA), .Q(R8_q), .clk(demultiplexer_1_out8));  // open: en, clr
  Register #(.width(16)) Rb (.D(DATA), .Q(Rb_q), .clk(demultiplexer_1_out11));  // open: en, clr
  Register #(.width(16)) Re (.D(DATA), .Q(Re_q), .clk(demultiplexer_1_out14));  // open: en, clr
  Register #(.width(16)) Rf (.D(DATA), .Q(Rf_q), .clk(demultiplexer_1_out15));  // open: en, clr
  Multiplexer #(.select(4), .width(16)) multiplexer_1 (
    .in0(R0_q), .in1(R1_q), .in2(R2_q), .in3(R3_q), .in4(R4_q), .in5(R5_q), .in6(R6_q), .in7(R7_q),
    .in8(R8_q), .in9(R9_q), .in10(Ra_q), .in11(Rb_q), .in12(Rc_q), .in13(Rd_q), .in14(Re_q), .in15(Rf_q),
    .out(out_6), .sel(Rx));  // open: en
  Multiplexer #(.select(4), .width(16)) multiplexer_2 (
    .in0(R0_q), .in1(R1_q), .in2(R2_q), .in3(R3_q), .in4(R4_q), .in5(R5_q), .in6(R6_q), .in7(R8_q),
    .in8(R8_q), .in9(R9_q), .in10(Ra_q), .in11(Rb_q), .in12(Rc_q), .in13(Rd_q), .in14(Re_q), .in15(Rf_q),
    .out(out_7), .sel(Ry));  // open: en
endmodule
